# Fritzing sketch Fritzing (saved by Fritzing 0.9.5d)

parts:
  A1 = DORHEA ESP32 GPIO breakout board 30pin
  M1 = PH meter with sensor in breadboard [package=THT]
  A2 = tds-sensor-meter-v1.0_1
  U1 = Turbidity Sensor Probe [package=THT]
  DS1 = DS18B20 1-Wire Temperature Sensor Probe  # not connected
  CPU1 = NodeMCU WROOM ESP 32  # not connected

nets:
  N1: A1.Pin_4, M1.pin1
  N2: A1.Pin_7, A2.pin1
  N3: A1.Pin_8, U1.VCC
  N4: A1.Pin_27, A1.Pin_58, M1.pin3
  N5: A1.Pin_61, A1.Pin_62, M1.pin2

custom parts:
  DORHEA ESP32 GPIO breakout board 30pin: ESP32 shield 30P expansion board, supports two power supply : DC 6.5-16v and USB 5.V
  PH meter with sensor in breadboard: DFrobot PH meter (SKU SEN0161)
  : TDS Meter V1.0 Development Board Water Meter Filter Measuring Water Sensor Module.
  Turbidity Sensor Probe: Turbidity sensor probe to the DFRobot measure module.
  NodeMCU WROOM ESP 32: 30 pol Development Kit
